// Logisim project [FINAL] Logisim Design.circ as structural Verilog: 11 circuits, main circuit main
// H. Adder
module _1_Bit_Half_Adder (
  input  A,
  input  B,
  output Sum,
  output Carry
);

  xor xor_1 (Sum, A, B);
  and and_1 (Carry, A, B);
endmodule

// F. Adder
module _1_Bit_Full_Adder (
  input  A,
  input  B,
  input  CarryIn,
  output Sum,
  output CarryOut
);

  wire Half_Adder_2_carry, Half_Adder_carry, Half_Adder_sum;

  _1_Bit_Half_Adder Half_Adder (.A(A), .B(B), .Sum(Half_Adder_sum), .Carry(Half_Adder_carry));
  _1_Bit_Half_Adder Half_Adder_2 (.A(Half_Adder_sum), .B(CarryIn), .Sum(Sum), .Carry(Half_Adder_2_carry));
  xor Xor (CarryOut, Half_Adder_2_carry, Half_Adder_carry);

  // Notes on the sheet:
  //   Sum(A+B)
  //   Carry(A+B)
endmodule

// +
module _16_Bit_Adder (
  input  [15:0] Input1,
  input  [15:0] Input2,
  output CarryOut,
  output [15:0] Output
);

  wire n1_bit_full_adder_1_carryout, n1_bit_full_adder_2_carryout, n1_bit_full_adder_3_carryout,
       n1_bit_full_adder_4_carryout, n1_bit_full_adder_5_carryout, n1_bit_full_adder_6_carryout,
       n1_bit_full_adder_7_carryout, n1_bit_full_adder_8_carryout, n1_bit_full_adder_9_carryout,
       n1_bit_full_adder_10_carryout, n1_bit_full_adder_11_carryout, n1_bit_full_adder_12_carryout,
       n1_bit_full_adder_13_carryout, n1_bit_full_adder_14_carryout, n1_bit_half_adder_1_carry;

  _1_Bit_Half_Adder u_1_bit_half_adder_1 (
    .A(Input2[0]), .B(Input1[0]), .Sum(Output[0]), .Carry(n1_bit_half_adder_1_carry));
  _1_Bit_Full_Adder u_1_bit_full_adder_1 (
    .A(Input2[1]), .B(Input1[1]), .CarryIn(n1_bit_half_adder_1_carry), .Sum(Output[1]),
    .CarryOut(n1_bit_full_adder_1_carryout));
  _1_Bit_Full_Adder u_1_bit_full_adder_2 (
    .A(Input2[2]), .B(Input1[2]), .CarryIn(n1_bit_full_adder_1_carryout), .Sum(Output[2]),
    .CarryOut(n1_bit_full_adder_2_carryout));
  _1_Bit_Full_Adder u_1_bit_full_adder_3 (
    .A(Input2[3]), .B(Input1[3]), .CarryIn(n1_bit_full_adder_2_carryout), .Sum(Output[3]),
    .CarryOut(n1_bit_full_adder_3_carryout));
  _1_Bit_Full_Adder u_1_bit_full_adder_4 (
    .A(Input2[4]), .B(Input1[4]), .CarryIn(n1_bit_full_adder_3_carryout), .Sum(Output[4]),
    .CarryOut(n1_bit_full_adder_4_carryout));
  _1_Bit_Full_Adder u_1_bit_full_adder_5 (
    .A(Input2[5]), .B(Input1[5]), .CarryIn(n1_bit_full_adder_4_carryout), .Sum(Output[5]),
    .CarryOut(n1_bit_full_adder_5_carryout));
  _1_Bit_Full_Adder u_1_bit_full_adder_6 (
    .A(Input2[6]), .B(Input1[6]), .CarryIn(n1_bit_full_adder_5_carryout), .Sum(Output[6]),
    .CarryOut(n1_bit_full_adder_6_carryout));
  _1_Bit_Full_Adder u_1_bit_full_adder_7 (
    .A(Input2[7]), .B(Input1[7]), .CarryIn(n1_bit_full_adder_6_carryout), .Sum(Output[7]),
    .CarryOut(n1_bit_full_adder_7_carryout));
  _1_Bit_Full_Adder u_1_bit_full_adder_8 (
    .A(Input2[8]), .B(Input1[8]), .CarryIn(n1_bit_full_adder_7_carryout), .Sum(Output[8]),
    .CarryOut(n1_bit_full_adder_8_carryout));
  _1_Bit_Full_Adder u_1_bit_full_adder_9 (
    .A(Input2[9]), .B(Input1[9]), .CarryIn(n1_bit_full_adder_8_carryout), .Sum(Output[9]),
    .CarryOut(n1_bit_full_adder_9_carryout));
  _1_Bit_Full_Adder u_1_bit_full_adder_10 (
    .A(Input2[10]), .B(Input1[10]), .CarryIn(n1_bit_full_adder_9_carryout), .Sum(Output[10]),
    .CarryOut(n1_bit_full_adder_10_carryout));
  _1_Bit_Full_Adder u_1_bit_full_adder_11 (
    .A(Input2[11]), .B(Input1[11]), .CarryIn(n1_bit_full_adder_10_carryout), .Sum(Output[11]),
    .CarryOut(n1_bit_full_adder_11_carryout));
  _1_Bit_Full_Adder u_1_bit_full_adder_12 (
    .A(Input2[12]), .B(Input1[12]), .CarryIn(n1_bit_full_adder_11_carryout), .Sum(Output[12]),
    .CarryOut(n1_bit_full_adder_12_carryout));
  _1_Bit_Full_Adder u_1_bit_full_adder_13 (
    .A(Input2[13]), .B(Input1[13]), .CarryIn(n1_bit_full_adder_12_carryout), .Sum(Output[13]),
    .CarryOut(n1_bit_full_adder_13_carryout));
  _1_Bit_Full_Adder u_1_bit_full_adder_14 (
    .A(Input2[14]), .B(Input1[14]), .CarryIn(n1_bit_full_adder_13_carryout), .Sum(Output[14]),
    .CarryOut(n1_bit_full_adder_14_carryout));
  _1_Bit_Full_Adder u_1_bit_full_adder_15 (
    .A(Input2[15]), .B(Input1[15]), .CarryIn(n1_bit_full_adder_14_carryout), .Sum(Output[15]),
    .CarryOut(CarryOut));
endmodule

// ALU
module ARITHMETIC_LOGIC_UNIT (
  input  [15:0] Input1,
  input  [15:0] Input2,
  input  [1:0] ALUSelect,
  output [15:0] Output
);

  wire [15:0] And_out, n16_bit_adder_1_output, Or_out;

  assign Or_out = Input1 | Input2;  // OR_Gate Or, 16 bits wide
  assign And_out = Input1 & Input2;  // AND_Gate And, 16 bits wide
  _16_Bit_Adder u_16_bit_adder_1 (.Input1(Input1), .Input2(Input2), .Output(n16_bit_adder_1_output));  // open: CarryOut
  Multiplexer #(.select(2), .width(16), .enable("false")) multiplexer_1 (
    .in0({16{1'b0}}), .in1(Or_out), .in2(And_out), .in3(n16_bit_adder_1_output), .out(Output), .sel(ALUSelect));

  // Notes on the sheet:
  //   Arithmetic Logic Unit
endmodule

module D_Latch_W__Async_Reset (
  input  D,
  input  Clock,
  input  Reset,
  output Q,
  output Q_prime
);

  wire nand_1_out, nand_2_out, not_1_out, not_2_out;

  not not_1 (not_1_out, D);
  nand nand_1 (nand_1_out, D, Clock);
  nand nand_2 (nand_2_out, Clock, not_1_out);
  not not_2 (not_2_out, Reset);
  nand nand_3 (Q, nand_1_out, Q_prime);
  nand nand_4 (Q_prime, Q, nand_2_out, not_2_out);

  // Notes on the sheet:
  //   Q: pull=up
endmodule

// DFF
module D_Flip_Flop (
  input  D,
  input  Clock,
  input  Reset,
  output out_4
);

  wire Master_q, not_1_out;

  not not_1 (not_1_out, Clock);
  D_Latch_W__Async_Reset Master (.D(D), .Clock(not_1_out), .Reset(Reset), .Q(Master_q));  // open: Q_prime
  D_Latch_W__Async_Reset Slave (.D(Master_q), .Clock(Clock), .Reset(Reset), .Q(out_4));  // open: Q_prime
endmodule

// 1-Bit
module _1_Bit_Register (
  input  I,
  input  Clock,
  input  Reset,
  output Q
);

  D_Flip_Flop d_flip_flop_1 (.D(I), .Clock(Clock), .Reset(Reset), .out_4(Q));
endmodule

// 16-Bit
module _16_Bit_Register (
  input  [15:0] In,
  input  Load,
  input  Reset,
  input  Clk,
  output [15:0] Out
);

  wire [15:0] multiplexer_1_out;

  Multiplexer #(.width(16), .enable("false")) multiplexer_1 (.in0(Out), .in1(In), .out(multiplexer_1_out), .sel(Load));
  _1_Bit_Register u_1_bit_register_1 (.Clock(Clk), .I(multiplexer_1_out[0]), .Reset(Reset), .Q(Out[0]));
  _1_Bit_Register u_1_bit_register_2 (.Clock(Clk), .I(multiplexer_1_out[1]), .Reset(Reset), .Q(Out[1]));
  _1_Bit_Register u_1_bit_register_3 (.Clock(Clk), .I(multiplexer_1_out[2]), .Reset(Reset), .Q(Out[2]));
  _1_Bit_Register u_1_bit_register_4 (.Clock(Clk), .I(multiplexer_1_out[3]), .Reset(Reset), .Q(Out[3]));
  _1_Bit_Register u_1_bit_register_5 (.Clock(Clk), .I(multiplexer_1_out[4]), .Reset(Reset), .Q(Out[4]));
  _1_Bit_Register u_1_bit_register_6 (.Clock(Clk), .I(multiplexer_1_out[5]), .Reset(Reset), .Q(Out[5]));
  _1_Bit_Register u_1_bit_register_7 (.Clock(Clk), .I(multiplexer_1_out[6]), .Reset(Reset), .Q(Out[6]));
  _1_Bit_Register u_1_bit_register_8 (.Clock(Clk), .I(multiplexer_1_out[7]), .Reset(Reset), .Q(Out[7]));
  _1_Bit_Register u_1_bit_register_9 (.Clock(Clk), .I(multiplexer_1_out[8]), .Reset(Reset), .Q(Out[8]));
  _1_Bit_Register u_1_bit_register_10 (.Clock(Clk), .I(multiplexer_1_out[9]), .Reset(Reset), .Q(Out[9]));
  _1_Bit_Register u_1_bit_register_11 (.Clock(Clk), .I(multiplexer_1_out[10]), .Reset(Reset), .Q(Out[10]));
  _1_Bit_Register u_1_bit_register_12 (.Clock(Clk), .I(multiplexer_1_out[11]), .Reset(Reset), .Q(Out[11]));
  _1_Bit_Register u_1_bit_register_13 (.Clock(Clk), .I(multiplexer_1_out[12]), .Reset(Reset), .Q(Out[12]));
  _1_Bit_Register u_1_bit_register_14 (.Clock(Clk), .I(multiplexer_1_out[13]), .Reset(Reset), .Q(Out[13]));
  _1_Bit_Register u_1_bit_register_15 (.Clock(Clk), .I(multiplexer_1_out[14]), .Reset(Reset), .Q(Out[14]));
  _1_Bit_Register u_1_bit_register_16 (.Clock(Clk), .I(multiplexer_1_out[15]), .Reset(Reset), .Q(Out[15]));
  // Probe on Out
  // Probe on Out

  // Notes on the sheet:
  //   0. Bit
  //   15. Bit
endmodule

// Reg. File
module REGISTER_FILE (
  input  [3:0] ReadAddr1,
  input  [3:0] ReadAddr2,
  input  [3:0] WriteAddr,
  input  [15:0] Input,
  input  WriteEnabled,
  input  Reset,
  input  Clk,
  output [15:0] Output1,
  output [15:0] Output2
);

  wire and_1_out, and_2_out, and_3_out, and_4_out, and_5_out, and_6_out, and_7_out, and_8_out, and_9_out,
       and_10_out, and_11_out, and_12_out, and_13_out, and_14_out, and_15_out, and_16_out, decoder_1_out0,
       decoder_1_out1, decoder_1_out2, decoder_1_out3, decoder_1_out4, decoder_1_out5, decoder_1_out6,
       decoder_1_out7, decoder_1_out8, decoder_1_out9, decoder_1_out10, decoder_1_out11, decoder_1_out12,
       decoder_1_out13, decoder_1_out14, decoder_1_out15, decoder_2_out0, decoder_2_out1, decoder_2_out2,
       decoder_2_out3, decoder_2_out4, decoder_2_out5, decoder_2_out6, decoder_2_out7, decoder_2_out8,
       decoder_2_out9, decoder_2_out10, decoder_2_out11, decoder_2_out12, decoder_2_out13, decoder_2_out14,
       decoder_2_out15, decoder_3_out0, decoder_3_out1, decoder_3_out2, decoder_3_out3, decoder_3_out4,
       decoder_3_out5, decoder_3_out6, decoder_3_out7, decoder_3_out8, decoder_3_out9, decoder_3_out10,
       decoder_3_out11, decoder_3_out12, decoder_3_out13, decoder_3_out14, decoder_3_out15;
  wire [15:0] n16_bit_register_1_out, n16_bit_register_2_out, n16_bit_register_3_out, n16_bit_register_4_out,
       n16_bit_register_5_out, n16_bit_register_6_out, n16_bit_register_7_out, n16_bit_register_8_out,
       n16_bit_register_9_out, n16_bit_register_10_out, n16_bit_register_11_out, n16_bit_register_12_out,
       n16_bit_register_13_out, n16_bit_register_14_out, n16_bit_register_15_out, n16_bit_register_16_out;

  Decoder #(.select(4), .enable("false")) decoder_1 (
    .out0(decoder_1_out0), .out1(decoder_1_out1), .out2(decoder_1_out2), .out3(decoder_1_out3),
    .out4(decoder_1_out4), .out5(decoder_1_out5), .out6(decoder_1_out6), .out7(decoder_1_out7),
    .out8(decoder_1_out8), .out9(decoder_1_out9), .out10(decoder_1_out10), .out11(decoder_1_out11),
    .out12(decoder_1_out12), .out13(decoder_1_out13), .out14(decoder_1_out14), .out15(decoder_1_out15),
    .sel(ReadAddr1));
  Decoder #(.select(4), .enable("false")) decoder_2 (
    .out0(decoder_2_out0), .out1(decoder_2_out1), .out2(decoder_2_out2), .out3(decoder_2_out3),
    .out4(decoder_2_out4), .out5(decoder_2_out5), .out6(decoder_2_out6), .out7(decoder_2_out7),
    .out8(decoder_2_out8), .out9(decoder_2_out9), .out10(decoder_2_out10), .out11(decoder_2_out11),
    .out12(decoder_2_out12), .out13(decoder_2_out13), .out14(decoder_2_out14), .out15(decoder_2_out15),
    .sel(ReadAddr2));
  Decoder #(.select(4), .enable("false")) decoder_3 (
    .out0(decoder_3_out0), .out1(decoder_3_out1), .out2(decoder_3_out2), .out3(decoder_3_out3),
    .out4(decoder_3_out4), .out5(decoder_3_out5), .out6(decoder_3_out6), .out7(decoder_3_out7),
    .out8(decoder_3_out8), .out9(decoder_3_out9), .out10(decoder_3_out10), .out11(decoder_3_out11),
    .out12(decoder_3_out12), .out13(decoder_3_out13), .out14(decoder_3_out14), .out15(decoder_3_out15),
    .sel(WriteAddr));
  and and_1 (and_1_out, WriteEnabled, decoder_3_out0);
  and and_2 (and_2_out, WriteEnabled, decoder_3_out1);
  and and_3 (and_3_out, WriteEnabled, decoder_3_out2);
  and and_4 (and_4_out, WriteEnabled, decoder_3_out3);
  and and_5 (and_5_out, WriteEnabled, decoder_3_out4);
  and and_6 (and_6_out, WriteEnabled, decoder_3_out5);
  and and_7 (and_7_out, WriteEnabled, decoder_3_out6);
  and and_8 (and_8_out, WriteEnabled, decoder_3_out7);
  and and_9 (and_9_out, WriteEnabled, decoder_3_out8);
  and and_10 (and_10_out, WriteEnabled, decoder_3_out9);
  and and_11 (and_11_out, WriteEnabled, decoder_3_out10);
  and and_12 (and_12_out, WriteEnabled, decoder_3_out11);
  and and_13 (and_13_out, WriteEnabled, decoder_3_out12);
  and and_14 (and_14_out, WriteEnabled, decoder_3_out13);
  and and_15 (and_15_out, WriteEnabled, decoder_3_out14);
  and and_16 (and_16_out, WriteEnabled, decoder_3_out15);
  _16_Bit_Register u_16_bit_register_1 (
    .Out(n16_bit_register_1_out), .Load(and_1_out), .Reset(Reset), .Clk(Clk), .In(Input));
  _16_Bit_Register u_16_bit_register_2 (
    .Out(n16_bit_register_2_out), .Load(and_2_out), .Reset(Reset), .Clk(Clk), .In(Input));
  _16_Bit_Register u_16_bit_register_3 (
    .Out(n16_bit_register_3_out), .Load(and_3_out), .Reset(Reset), .Clk(Clk), .In(Input));
  _16_Bit_Register u_16_bit_register_4 (
    .Out(n16_bit_register_4_out), .Load(and_4_out), .Reset(Reset), .Clk(Clk), .In(Input));
  _16_Bit_Register u_16_bit_register_5 (
    .Out(n16_bit_register_5_out), .Load(and_5_out), .Reset(Reset), .Clk(Clk), .In(Input));
  _16_Bit_Register u_16_bit_register_6 (
    .Out(n16_bit_register_6_out), .Load(and_6_out), .Reset(Reset), .Clk(Clk), .In(Input));
  _16_Bit_Register u_16_bit_register_7 (
    .Out(n16_bit_register_7_out), .Load(and_7_out), .Reset(Reset), .Clk(Clk), .In(Input));
  _16_Bit_Register u_16_bit_register_8 (
    .Out(n16_bit_register_8_out), .Load(and_8_out), .Reset(Reset), .Clk(Clk), .In(Input));
  _16_Bit_Register u_16_bit_register_9 (
    .Out(n16_bit_register_9_out), .Load(and_9_out), .Reset(Reset), .Clk(Clk), .In(Input));
  _16_Bit_Register u_16_bit_register_10 (
    .Out(n16_bit_register_10_out), .Load(and_10_out), .Reset(Reset), .Clk(Clk), .In(Input));
  _16_Bit_Register u_16_bit_register_11 (
    .Out(n16_bit_register_11_out), .Load(and_11_out), .Reset(Reset), .Clk(Clk), .In(Input));
  _16_Bit_Register u_16_bit_register_12 (
    .Out(n16_bit_register_12_out), .Load(and_12_out), .Reset(Reset), .Clk(Clk), .In(Input));
  _16_Bit_Register u_16_bit_register_13 (
    .Out(n16_bit_register_13_out), .Load(and_13_out), .Reset(Reset), .Clk(Clk), .In(Input));
  _16_Bit_Register u_16_bit_register_14 (
    .Out(n16_bit_register_14_out), .Load(and_14_out), .Reset(Reset), .Clk(Clk), .In(Input));
  _16_Bit_Register u_16_bit_register_15 (
    .Out(n16_bit_register_15_out), .Load(and_15_out), .Reset(Reset), .Clk(Clk), .In(Input));
  _16_Bit_Register u_16_bit_register_16 (
    .Out(n16_bit_register_16_out), .Load(and_16_out), .Reset(Reset), .Clk(Clk), .In(Input));
  assign Output1 = decoder_1_out0 ? n16_bit_register_1_out : 16'bz;  // Controlled_Buffer controlled_buffer_1
  assign Output1 = decoder_1_out1 ? n16_bit_register_2_out : 16'bz;  // Controlled_Buffer controlled_buffer_2
  assign Output1 = decoder_1_out2 ? n16_bit_register_3_out : 16'bz;  // Controlled_Buffer controlled_buffer_3
  assign Output1 = decoder_1_out3 ? n16_bit_register_4_out : 16'bz;  // Controlled_Buffer controlled_buffer_4
  assign Output1 = decoder_1_out4 ? n16_bit_register_5_out : 16'bz;  // Controlled_Buffer controlled_buffer_5
  assign Output1 = decoder_1_out5 ? n16_bit_register_6_out : 16'bz;  // Controlled_Buffer controlled_buffer_6
  assign Output1 = decoder_1_out6 ? n16_bit_register_7_out : 16'bz;  // Controlled_Buffer controlled_buffer_7
  assign Output1 = decoder_1_out7 ? n16_bit_register_8_out : 16'bz;  // Controlled_Buffer controlled_buffer_8
  assign Output1 = decoder_1_out8 ? n16_bit_register_9_out : 16'bz;  // Controlled_Buffer controlled_buffer_9
  assign Output1 = decoder_1_out9 ? n16_bit_register_10_out : 16'bz;  // Controlled_Buffer controlled_buffer_10
  assign Output1 = decoder_1_out10 ? n16_bit_register_11_out : 16'bz;  // Controlled_Buffer controlled_buffer_11
  assign Output1 = decoder_1_out11 ? n16_bit_register_12_out : 16'bz;  // Controlled_Buffer controlled_buffer_12
  assign Output1 = decoder_1_out12 ? n16_bit_register_13_out : 16'bz;  // Controlled_Buffer controlled_buffer_13
  assign Output1 = decoder_1_out13 ? n16_bit_register_14_out : 16'bz;  // Controlled_Buffer controlled_buffer_14
  assign Output1 = decoder_1_out14 ? n16_bit_register_15_out : 16'bz;  // Controlled_Buffer controlled_buffer_15
  assign Output1 = decoder_1_out15 ? n16_bit_register_16_out : 16'bz;  // Controlled_Buffer controlled_buffer_16
  assign Output2 = decoder_2_out0 ? n16_bit_register_1_out : 16'bz;  // Controlled_Buffer controlled_buffer_17
  assign Output2 = decoder_2_out1 ? n16_bit_register_2_out : 16'bz;  // Controlled_Buffer controlled_buffer_18
  assign Output2 = decoder_2_out2 ? n16_bit_register_3_out : 16'bz;  // Controlled_Buffer controlled_buffer_19
  assign Output2 = decoder_2_out3 ? n16_bit_register_4_out : 16'bz;  // Controlled_Buffer controlled_buffer_20
  assign Output2 = decoder_2_out4 ? n16_bit_register_5_out : 16'bz;  // Controlled_Buffer controlled_buffer_21
  assign Output2 = decoder_2_out5 ? n16_bit_register_6_out : 16'bz;  // Controlled_Buffer controlled_buffer_22
  assign Output2 = decoder_2_out6 ? n16_bit_register_7_out : 16'bz;  // Controlled_Buffer controlled_buffer_23
  assign Output2 = decoder_2_out7 ? n16_bit_register_8_out : 16'bz;  // Controlled_Buffer controlled_buffer_24
  assign Output2 = decoder_2_out8 ? n16_bit_register_9_out : 16'bz;  // Controlled_Buffer controlled_buffer_25
  assign Output2 = decoder_2_out9 ? n16_bit_register_10_out : 16'bz;  // Controlled_Buffer controlled_buffer_26
  assign Output2 = decoder_2_out10 ? n16_bit_register_11_out : 16'bz;  // Controlled_Buffer controlled_buffer_27
  assign Output2 = decoder_2_out11 ? n16_bit_register_12_out : 16'bz;  // Controlled_Buffer controlled_buffer_28
  assign Output2 = decoder_2_out12 ? n16_bit_register_13_out : 16'bz;  // Controlled_Buffer controlled_buffer_29
  assign Output2 = decoder_2_out13 ? n16_bit_register_14_out : 16'bz;  // Controlled_Buffer controlled_buffer_30
  assign Output2 = decoder_2_out14 ? n16_bit_register_15_out : 16'bz;  // Controlled_Buffer controlled_buffer_31
  assign Output2 = decoder_2_out15 ? n16_bit_register_16_out : 16'bz;  // Controlled_Buffer controlled_buffer_32

  // Notes on the sheet:
  //   Register File
endmodule

// Control Unit
module CONTROL_UNIT (
  input  [15:0] CU_Input,
  input  [8:0] StackPointer,
  input  Clk,
  input  Reset,
  output PCSelect,
  output SPSelect,
  output RegWrite,
  output MemWrite,
  output MemRead,
  output RegWriteSelect,
  output Store,
  output ImmSelect,
  output [1:0] ALUSelect,
  output [12:0] JumpAddr,
  output [3:0] DR,
  output [8:0] Ld_StAddr,
  output [3:0] SR1,
  output [3:0] SR2_Imm,
  output InstRegWrite,
  output PCWrite,
  output SPWrite
);

  wire and_4_out, decoder_1_out1, decoder_1_out2, decoder_1_out3, decoder_1_out4, decoder_1_out7, not_1_out,
       or_1_out, or_2_out, or_3_out, or_4_out, or_6_out;

  not not_1 (not_1_out, PCWrite);
  D_Flip_Flop d_flip_flop_1 (.D(not_1_out), .Clock(Clk), .Reset(Reset), .out_4(PCWrite));
  not not_2 (InstRegWrite, PCWrite);
  Multiplexer #(.width(4), .enable("false")) multiplexer_1 (
    .in0(CU_Input[8:5]), .in1(CU_Input[12:9]), .out(SR1), .sel(or_6_out));
  Decoder #(.select(3), .enable("false")) decoder_1 (
    .out0(PCSelect), .out1(decoder_1_out1), .out2(decoder_1_out2), .out3(decoder_1_out3),
    .out4(decoder_1_out4), .out5(Store), .out6(SPSelect), .out7(decoder_1_out7), .sel(CU_Input[15:13]));
  and and_1 (RegWrite, PCWrite, or_1_out);
  or or_1 (or_1_out, decoder_1_out1, decoder_1_out2, decoder_1_out3, decoder_1_out4, decoder_1_out7);
  and and_2 (MemWrite, PCWrite, or_2_out);
  or or_2 (or_2_out, Store, SPSelect);
  and and_3 (MemRead, PCWrite, or_3_out);
  or or_3 (or_3_out, decoder_1_out4, decoder_1_out7);
  or or_4 (or_4_out, StackPointer[8], StackPointer[7], StackPointer[6], StackPointer[5], StackPointer[4], StackPointer[3], StackPointer[2], StackPointer[1], StackPointer[0]);
  and and_4 (and_4_out, or_4_out, decoder_1_out7);
  and and_5 (SPWrite, PCWrite, or_6_out);
  or or_5 (RegWriteSelect, decoder_1_out4, decoder_1_out7);
  or or_6 (or_6_out, and_4_out, SPSelect);

  assign ALUSelect = CU_Input[14:13];
  assign DR = CU_Input[12:9];
  assign ImmSelect = CU_Input[0];
  assign JumpAddr = CU_Input[12:0];
  assign Ld_StAddr = CU_Input[8:0];
  assign SR2_Imm = CU_Input[4:1];

  // Notes on the sheet:
  //   Control Unit
  //   JUMP
  //   OR/ORI
  //   AND/ANDI
  //   ADD/ADDI
  //   LD
  //   ST
  //   PUSH
  //   POP
endmodule

module main (
  input  Reset
);

  wire Clk, control_unit_1_immselect, control_unit_1_instregwrite, control_unit_1_memread,
       control_unit_1_memwrite, control_unit_1_pcselect, control_unit_1_pcwrite, control_unit_1_regwrite,
       control_unit_1_regwriteselect, control_unit_1_spselect, control_unit_1_spwrite, control_unit_1_store,
       not_1_out;
  wire [1:0] control_unit_1_aluselect;
  wire [3:0] control_unit_1_dr, control_unit_1_sr1, control_unit_1_sr2_imm, multiplexer_6_out;
  wire [8:0] bit_extender_2_out, control_unit_1_ld_staddr;
  wire [9:0] bit_extender_1_out, bit_extender_3_out, bit_extender_6_out, multiplexer_1_out;
  wire [12:0] control_unit_1_jumpaddr;
  wire [15:0] ALUOutput, bit_extender_4_out, bit_extender_5_out, Instruction_Register_out, multiplexer_2_out,
       multiplexer_3_out, multiplexer_4_out, multiplexer_5_out, multiplexer_7_out, n16_bit_adder_1_output,
       n16_bit_adder_2_output, n16_bit_adder_3_output, n16_bit_adder_4_output, not_2_out,
       Program_Counter_out, ram_1_data, register_file_1_output2, RegOut1, rom_1_data, Stack_Pointer_out;

  Clock u_Clk (.out(Clk));
  assign bit_extender_1_out = {{1{1'b0}}, control_unit_1_ld_staddr};  // Bit_Extender bit_extender_1
  Multiplexer #(.width(10), .enable("false")) multiplexer_1 (
    .in0(bit_extender_1_out), .in1(bit_extender_3_out), .out(multiplexer_1_out), .sel(control_unit_1_spwrite));
  _16_Bit_Register Stack_Pointer (
    .Out(Stack_Pointer_out), .Load(control_unit_1_spwrite), .Reset(Reset), .Clk(Clk),
    .In(n16_bit_adder_1_output));
  Multiplexer #(.width(16), .enable("false")) multiplexer_2 (
    .in0({16{1'b1}}), .in1(16'h1), .out(multiplexer_2_out), .sel(control_unit_1_spselect));
  _16_Bit_Adder u_16_bit_adder_1 (
    .Input1(multiplexer_2_out), .Input2(Stack_Pointer_out), .Output(n16_bit_adder_1_output));  // open: CarryOut
  _16_Bit_Adder u_16_bit_adder_2 (
    .Input1({16{1'b1}}), .Input2(Stack_Pointer_out), .Output(n16_bit_adder_2_output));  // open: CarryOut
  // Probe on Stack_Pointer_out
  Multiplexer #(.width(16), .enable("false")) multiplexer_3 (
    .in0(ALUOutput), .in1(ram_1_data), .out(multiplexer_3_out), .sel(control_unit_1_regwriteselect));
  RAM #(.addrWidth(10), .dataWidth(16), .bus("separate")) ram_1 (
    .addr(multiplexer_1_out), .din(RegOut1), .data(ram_1_data), .str(control_unit_1_memwrite), .clk(Clk),
    .ld(control_unit_1_memread));  // open: sel, clr
  not not_1 (not_1_out, control_unit_1_spselect);
  assign not_2_out = ~multiplexer_4_out;  // NOT_Gate not_2, 16 bits wide
  Multiplexer #(.width(16), .enable("false")) multiplexer_4 (
    .in0(Stack_Pointer_out), .in1(n16_bit_adder_2_output), .out(multiplexer_4_out), .sel(not_1_out));
  Bit_Extender #(.in_width(16), .out_width(9)) bit_extender_2 (.in(Stack_Pointer_out), .out(bit_extender_2_out));
  Bit_Extender #(.in_width(16), .out_width(10), .\type ("sign")) bit_extender_3 (
    .in(not_2_out), .out(bit_extender_3_out));
  REGISTER_FILE register_file_1 (
    .WriteEnabled(control_unit_1_regwrite), .Input(multiplexer_3_out), .Clk(Clk),
    .WriteAddr(control_unit_1_dr), .ReadAddr2(control_unit_1_sr2_imm), .ReadAddr1(multiplexer_6_out),
    .Reset(Reset), .Output1(RegOut1), .Output2(register_file_1_output2));
  CONTROL_UNIT control_unit_1 (
    .CU_Input(Instruction_Register_out), .ImmSelect(control_unit_1_immselect),
    .JumpAddr(control_unit_1_jumpaddr), .Ld_StAddr(control_unit_1_ld_staddr),
    .ALUSelect(control_unit_1_aluselect), .DR(control_unit_1_dr), .SR1(control_unit_1_sr1),
    .SR2_Imm(control_unit_1_sr2_imm), .PCSelect(control_unit_1_pcselect), .MemWrite(control_unit_1_memwrite),
    .MemRead(control_unit_1_memread), .StackPointer(bit_extender_2_out), .SPWrite(control_unit_1_spwrite),
    .InstRegWrite(control_unit_1_instregwrite), .Reset(Reset), .Clk(Clk),
    .RegWriteSelect(control_unit_1_regwriteselect), .PCWrite(control_unit_1_pcwrite),
    .SPSelect(control_unit_1_spselect), .RegWrite(control_unit_1_regwrite), .Store(control_unit_1_store));
  Multiplexer #(.width(16), .enable("false")) multiplexer_5 (
    .in0({16{1'b0}}), .in1(bit_extender_4_out), .out(multiplexer_5_out), .sel(control_unit_1_pcselect));
  assign bit_extender_4_out = {{3{control_unit_1_jumpaddr[12]}}, control_unit_1_jumpaddr};  // Bit_Extender bit_extender_4
  _16_Bit_Register Program_Counter (
    .Out(Program_Counter_out), .Load(control_unit_1_pcwrite), .Reset(Reset), .Clk(Clk),
    .In(n16_bit_adder_4_output));
  Multiplexer #(.width(4), .enable("false")) multiplexer_6 (
    .in0(control_unit_1_sr1), .in1(control_unit_1_dr), .out(multiplexer_6_out), .sel(control_unit_1_store));
  _16_Bit_Adder u_16_bit_adder_3 (
    .Input1(multiplexer_5_out), .Input2(16'h1), .Output(n16_bit_adder_3_output));  // open: CarryOut
  // Probe on Program_Counter_out
  _16_Bit_Adder u_16_bit_adder_4 (
    .Input1(n16_bit_adder_3_output), .Input2(Program_Counter_out), .Output(n16_bit_adder_4_output));  // open: CarryOut
  assign bit_extender_5_out = {{12{control_unit_1_sr2_imm[3]}}, control_unit_1_sr2_imm};  // Bit_Extender bit_extender_5
  Multiplexer #(.width(16), .enable("false")) multiplexer_7 (
    .in0(register_file_1_output2), .in1(bit_extender_5_out), .out(multiplexer_7_out),
    .sel(control_unit_1_immselect));
  ARITHMETIC_LOGIC_UNIT arithmetic_logic_unit_1 (
    .Input1(multiplexer_7_out), .Input2(RegOut1), .ALUSelect(control_unit_1_aluselect), .Output(ALUOutput));
  Bit_Extender #(.in_width(16), .out_width(10)) bit_extender_6 (.in(Program_Counter_out), .out(bit_extender_6_out));
  // Probe on ALUOutput
  // Probe on ALUOutput
  _16_Bit_Register Instruction_Register (
    .Out(Instruction_Register_out), .Load(control_unit_1_instregwrite), .Reset(Reset), .Clk(Clk),
    .In(rom_1_data));
  ROM #(.addrWidth(10), .dataWidth(16)) rom_1 (.addr(bit_extender_6_out), .data(rom_1_data));  // open: sel
  // Probe on Instruction_Register_out

  // Notes on the sheet:
  //   Data Memory
  //   Ld/StAddr
  //   MemWrite
  //   MemRead
  //   RegWrSelect
  //   SPWrite
  //   StackPointer -->
  //   SPSelect
  //   RegWrite
  //   Jump
  //   Address
  //   PCWrite
  //   Store
  //   DR
  //   ImmSelect
  //   SR1
  //   SR2/Imm
  //   ALUSelect
  //   PCMux
  //   <-- CUInput
  //   InstRegWrite
  //   ImmSelectMUX
  //   Instruction Memory
  //   contents of rom_1 (hex, n*v repeats v):
  //   8000 8202 8603 6420 c600 6646 a60a e600 666f 4802 4027 0 246b 2462
endmodule
